// Logisim project assign1.circ as structural Verilog: 1 circuit, main circuit main
module main (
  input  W,
  input  X,
  input  Y,
  input  Z
);

  wire A_out, B_out, C_out, D_out, E_out, F_out, G_out, not_1_out, not_2_out, not_3_out, not_4_out,
       W_prime_X_out, W_prime_X_prime_out, W_prime_X_prime_Z_prime_out, W_prime_XY_prime_2_out,
       W_prime_XY_prime_out, W_prime_XZ_out, W_prime_Y_out, W_prime_Y_prime_out, W_prime_Y_prime_Z_prime_out,
       W_prime_YZ_out, W_prime_Z_out, WX_out, WX_prime_2_out, WX_prime_3_out, WX_prime_out,
       WX_prime_Y_prime_out, WY_2_out, WY_out, WY_prime_out, WY_prime_Z_out, WZ_out, WZ_prime_out,
       X_prime_Y_out, X_prime_YZ_out, X_prime_Z_prime_2_out, X_prime_Z_prime_3_out, X_prime_Z_prime_out,
       XY_out, XY_prime_Z_out, XYZ_prime_out, XZ_prime_out, Y_prime_Z_out, Y_prime_Z_prime_out,
       YZ_prime_2_out, YZ_prime_out;

  not not_1 (not_1_out, W);
  not not_2 (not_2_out, X);
  not not_3 (not_3_out, Z);
  not not_4 (not_4_out, Y);
  and X_prime_Z_prime (X_prime_Z_prime_out, not_2_out, not_3_out);
  and WZ_prime (WZ_prime_out, W, not_3_out);
  and W_prime_Y (W_prime_Y_out, not_1_out, Y);
  and XY (XY_out, X, Y);
  and W_prime_XZ (W_prime_XZ_out, not_1_out, X, Z);
  and WX_prime_Y_prime (WX_prime_Y_prime_out, W, not_2_out, not_4_out);
  and X_prime_Z_prime_2 (X_prime_Z_prime_2_out, not_2_out, not_3_out);
  and W_prime_X_prime (W_prime_X_prime_out, not_1_out, not_2_out);
  and W_prime_Y_prime_Z_prime (W_prime_Y_prime_Z_prime_out, not_1_out, not_4_out, not_3_out);
  and W_prime_YZ (W_prime_YZ_out, not_1_out, Y, Z);
  and WY_prime_Z (WY_prime_Z_out, W, not_4_out, Z);
  and W_prime_Y_prime (W_prime_Y_prime_out, not_1_out, not_4_out);
  and W_prime_Z (W_prime_Z_out, not_1_out, Z);
  and Y_prime_Z (Y_prime_Z_out, not_4_out, Z);
  and W_prime_X (W_prime_X_out, not_1_out, X);
  and WX_prime (WX_prime_out, W, not_2_out);
  and W_prime_X_prime_Z_prime (W_prime_X_prime_Z_prime_out, not_1_out, not_2_out, not_3_out);
  and WY_prime (WY_prime_out, W, not_4_out);
  and XY_prime_Z (XY_prime_Z_out, X, not_4_out, Z);
  and X_prime_YZ (X_prime_YZ_out, not_2_out, Y, Z);
  and XYZ_prime (XYZ_prime_out, X, Y, not_3_out);
  and X_prime_Z_prime_3 (X_prime_Z_prime_3_out, not_2_out, not_3_out);
  and WX (WX_out, W, X);
  and YZ_prime (YZ_prime_out, Y, not_3_out);
  and WY (WY_out, W, Y);
  and Y_prime_Z_prime (Y_prime_Z_prime_out, not_4_out, not_3_out);
  and W_prime_XY_prime (W_prime_XY_prime_out, not_1_out, X, not_4_out);
  and XZ_prime (XZ_prime_out, X, not_3_out);
  and WX_prime_2 (WX_prime_2_out, W, not_2_out);
  and WY_2 (WY_2_out, W, Y);
  and X_prime_Y (X_prime_Y_out, not_2_out, Y);
  and W_prime_XY_prime_2 (W_prime_XY_prime_2_out, not_1_out, X, not_4_out);
  and YZ_prime_2 (YZ_prime_2_out, Y, not_3_out);
  and WX_prime_3 (WX_prime_3_out, W, not_2_out);
  and WZ (WZ_out, W, Z);
  or A (A_out, X_prime_Z_prime_out, WZ_prime_out, W_prime_Y_out, XY_out, W_prime_XZ_out, WX_prime_Y_prime_out);
  or B (B_out, X_prime_Z_prime_2_out, W_prime_X_prime_out, W_prime_Y_prime_Z_prime_out, W_prime_YZ_out, WY_prime_Z_out);
  or C (C_out, W_prime_Y_prime_out, W_prime_Z_out, Y_prime_Z_out, W_prime_X_out, WX_prime_out);
  or D (D_out, W_prime_X_prime_Z_prime_out, WY_prime_out, XY_prime_Z_out, X_prime_YZ_out, XYZ_prime_out);
  or E (E_out, X_prime_Z_prime_3_out, WX_out, YZ_prime_out, WY_out);
  or F (F_out, Y_prime_Z_prime_out, W_prime_XY_prime_out, XZ_prime_out, WX_prime_2_out, WY_2_out);
  or G (G_out, X_prime_Y_out, W_prime_XY_prime_2_out, YZ_prime_2_out, WX_prime_3_out, WZ_out);
  _7_Segment_Display u_7_segment_display_1 (
    .g(G_out), .f(F_out), .a(A_out), .b(B_out), .e(E_out), .d(D_out), .c(C_out));  // open: dp
endmodule
