// Logisim project assign1bonus.circ as structural Verilog: 1 circuit, main circuit main
module main (
);

  wire A_out, B_out, button_1_out, C_out, D_out, E_out, F_out, G_out, not_1_out, not_2_out, not_3_out,
       not_4_out, not_5_out, not_6_out, not_7_out, W_prime_X_out, W_prime_X_prime_out,
       W_prime_X_prime_Z_prime_out, W_prime_XY_prime_2_out, W_prime_XY_prime_out, W_prime_XZ_out,
       W_prime_Y_out, W_prime_Y_prime_out, W_prime_Y_prime_Z_prime_out, W_prime_YZ_out, W_prime_Z_out, W_q,
       WX_out, WX_prime_2_out, WX_prime_3_out, WX_prime_out, WX_prime_Y_prime_out, WY_2_out, WY_out,
       WY_prime_out, WY_prime_Z_out, WZ_out, WZ_prime_out, X_prime_Y_out, X_prime_YZ_out,
       X_prime_Z_prime_2_out, X_prime_Z_prime_3_out, X_prime_Z_prime_out, X_q, XY_out, XY_prime_Z_out,
       XYZ_prime_out, XZ_prime_out, Y_prime_Z_out, Y_prime_Z_prime_out, Y_q, YZ_prime_2_out, YZ_prime_out,
       Z_q;

  Counter #(.width(1), .max('h1)) W (.Q(W_q), .clk(not_3_out));  // open: load, D, count, carry, clr
  not not_1 (not_1_out, X_q);
  not not_2 (not_2_out, W_q);
  not not_3 (not_3_out, X_q);
  Counter #(.width(1), .max('h1)) X (.Q(X_q), .clk(not_6_out));  // open: load, D, count, carry, clr
  not not_4 (not_4_out, Z_q);
  not not_5 (not_5_out, Y_q);
  not not_6 (not_6_out, Y_q);
  Counter #(.width(1), .max('h1)) Y (.Q(Y_q), .clk(not_7_out));  // open: load, D, count, carry, clr
  Counter #(.width(1), .max('h1)) Z (.Q(Z_q), .clk(button_1_out));  // open: load, D, count, carry, clr
  and X_prime_Z_prime (X_prime_Z_prime_out, not_1_out, not_4_out);
  and W_prime_Y (W_prime_Y_out, not_2_out, Y_q);
  and W_prime_XZ (W_prime_XZ_out, not_2_out, X_q, Z_q);
  and X_prime_Z_prime_2 (X_prime_Z_prime_2_out, not_1_out, not_4_out);
  and W_prime_Y_prime_Z_prime (W_prime_Y_prime_Z_prime_out, not_2_out, not_5_out, not_4_out);
  and WY_prime_Z (WY_prime_Z_out, W_q, not_5_out, Z_q);
  and W_prime_Y_prime (W_prime_Y_prime_out, not_2_out, not_5_out);
  and Y_prime_Z (Y_prime_Z_out, not_5_out, Z_q);
  and WX_prime (WX_prime_out, W_q, not_1_out);
  and W_prime_X_prime_Z_prime (W_prime_X_prime_Z_prime_out, not_2_out, not_1_out, not_4_out);
  and XY_prime_Z (XY_prime_Z_out, X_q, not_5_out, Z_q);
  and XYZ_prime (XYZ_prime_out, X_q, Y_q, not_4_out);
  and X_prime_Z_prime_3 (X_prime_Z_prime_3_out, not_1_out, not_4_out);
  and YZ_prime (YZ_prime_out, Y_q, not_4_out);
  and Y_prime_Z_prime (Y_prime_Z_prime_out, not_5_out, not_4_out);
  and XZ_prime (XZ_prime_out, X_q, not_4_out);
  and WY (WY_out, W_q, Y_q);
  and X_prime_Y (X_prime_Y_out, not_1_out, Y_q);
  and YZ_prime_2 (YZ_prime_2_out, Y_q, not_4_out);
  and WZ (WZ_out, W_q, Z_q);
  not not_7 (not_7_out, Z_q);
  Button button_1 (.out(button_1_out));
  and WZ_prime (WZ_prime_out, W_q, not_4_out);
  and XY (XY_out, X_q, Y_q);
  and WX_prime_Y_prime (WX_prime_Y_prime_out, W_q, not_1_out, not_5_out);
  and W_prime_X_prime (W_prime_X_prime_out, not_2_out, not_1_out);
  and W_prime_YZ (W_prime_YZ_out, not_2_out, Y_q, Z_q);
  and W_prime_Z (W_prime_Z_out, not_2_out, Z_q);
  and W_prime_X (W_prime_X_out, not_2_out, X_q);
  and WY_prime (WY_prime_out, W_q, not_5_out);
  and X_prime_YZ (X_prime_YZ_out, not_1_out, Y_q, Z_q);
  and WX (WX_out, W_q, X_q);
  and WY_2 (WY_2_out, W_q, Y_q);
  and W_prime_XY_prime (W_prime_XY_prime_out, not_2_out, X_q, not_5_out);
  and WX_prime_2 (WX_prime_2_out, W_q, not_1_out);
  and W_prime_XY_prime_2 (W_prime_XY_prime_2_out, not_2_out, X_q, not_5_out);
  and WX_prime_3 (WX_prime_3_out, W_q, not_1_out);
  or A (A_out, X_prime_Z_prime_out, WZ_prime_out, W_prime_Y_out, XY_out, W_prime_XZ_out, WX_prime_Y_prime_out);
  or B (B_out, X_prime_Z_prime_2_out, W_prime_X_prime_out, W_prime_Y_prime_Z_prime_out, W_prime_YZ_out, WY_prime_Z_out);
  or C (C_out, W_prime_Y_prime_out, W_prime_Z_out, Y_prime_Z_out, W_prime_X_out, WX_prime_out);
  or D (D_out, W_prime_X_prime_Z_prime_out, WY_prime_out, XY_prime_Z_out, X_prime_YZ_out, XYZ_prime_out);
  or E (E_out, X_prime_Z_prime_3_out, WX_out, YZ_prime_out, WY_2_out);
  or F (F_out, Y_prime_Z_prime_out, W_prime_XY_prime_out, XZ_prime_out, WX_prime_2_out, WY_out);
  or G (G_out, X_prime_Y_out, W_prime_XY_prime_2_out, YZ_prime_2_out, WX_prime_3_out, WZ_out);
  _7_Segment_Display u_7_segment_display_1 (
    .g(G_out), .f(F_out), .a(A_out), .b(B_out), .e(E_out), .d(D_out), .c(C_out));  // open: dp

  // Notes on the sheet:
  //   PRESS ME
endmodule
