// Logisim project assign2.circ as structural Verilog: 1 circuit, main circuit main
module main (
  input  d,
  input  e
);

  wire A_q, A_qn, and_1_out, and_2_out, and_3_out, and_4_out, and_5_out, and_6_out, and_7_out, and_8_out,
       and_9_out, and_10_out, and_11_out, and_12_out, and_13_out, and_14_out, and_15_out, and_16_out, B_q,
       B_qn, C_q, C_qn, clock_1_out, not_1_out, not_2_out, or_1_out, or_2_out, or_3_out, or_4_out, or_5_out,
       or_6_out;

  not not_1 (not_1_out, d);
  not not_2 (not_2_out, e);
  Clock clock_1 (.out(clock_1_out));
  and and_1 (and_1_out, B_qn, C_qn, d, e);
  and and_2 (and_2_out, B_q, C_qn, not_1_out, e);
  and and_3 (and_3_out, B_qn, C_qn, not_1_out, e);
  and and_4 (and_4_out, B_q, C_qn, d, e);
  and and_5 (and_5_out, A_qn, C_q, not_1_out, e);
  and and_6 (and_6_out, A_q, C_q, d, e);
  and and_7 (and_7_out, A_qn, C_q, d, e);
  and and_8 (and_8_out, A_q, C_q, not_1_out, e);
  and and_9 (and_9_out, A_qn, B_qn, not_1_out, e);
  and and_10 (and_10_out, A_qn, B_q, d, e);
  and and_11 (and_11_out, A_q, B_qn, d, e);
  and and_12 (and_12_out, A_q, B_q, not_1_out, e);
  and and_13 (and_13_out, A_qn, B_qn, d, e);
  and and_14 (and_14_out, A_qn, B_q, not_1_out, e);
  and and_15 (and_15_out, A_q, B_qn, not_1_out, e);
  and and_16 (and_16_out, A_q, B_q, d, e);
  or or_1 (or_1_out, and_1_out, and_2_out);
  or or_2 (or_2_out, and_3_out, and_4_out);
  or or_3 (or_3_out, and_5_out, and_6_out);
  or or_4 (or_4_out, and_7_out, and_8_out);
  or or_5 (or_5_out, and_9_out, and_10_out, and_11_out, and_12_out);
  or or_6 (or_6_out, and_13_out, and_14_out, and_15_out, and_16_out);
  J_K_Flip_Flop A (.J(or_1_out), .clk(clock_1_out), .K(or_2_out), .Q(A_q), .Qn(A_qn));  // open: preset, en, reset
  J_K_Flip_Flop B (.J(or_3_out), .clk(clock_1_out), .K(or_4_out), .Q(B_q), .Qn(B_qn));  // open: preset, en, reset
  J_K_Flip_Flop C (.J(or_5_out), .clk(clock_1_out), .K(or_6_out), .Q(C_q), .Qn(C_qn));  // open: preset, en, reset
  LED led_1 (.in(A_q));
  LED led_2 (.in(B_q));
  LED led_3 (.in(C_q));
endmodule
