// Logisim project assign2bonus.circ as structural Verilog: 1 circuit, main circuit main
module main (
  input  d,
  input  e
);

  wire A_q, A_qn, and_1_out, and_2_out, and_3_out, and_4_out, and_5_out, and_6_out, and_7_out, and_8_out,
       and_9_out, and_10_out, and_11_out, and_12_out, and_13_out, and_14_out, and_15_out, and_16_out, B_q,
       B_qn, C_q, C_qn, clock_1_out, not_1_out, not_2_out, or_1_out, or_2_out, or_3_out;

  not not_1 (not_1_out, d);
  Clock clock_1 (.out(clock_1_out));
  not not_2 (not_2_out, e);
  and and_1 (and_1_out, A_qn, B_qn, C_qn, d, e);
  and and_2 (and_2_out, A_qn, B_q, C_qn, not_1_out, e);
  and and_3 (and_3_out, A_q, B_qn, C_qn, not_1_out, e);
  and and_4 (and_4_out, A_q, B_q, C_qn, d, e);
  and and_5 (and_5_out, A_qn, B_qn, C_q, not_1_out, e);
  and and_6 (and_6_out, A_qn, B_q, C_q, d, e);
  and and_7 (and_7_out, A_q, B_qn, C_q, d, e);
  and and_8 (and_8_out, A_q, B_q, C_q, not_1_out, e);
  and and_9 (and_9_out, A_qn, B_qn, C_qn, not_1_out, e);
  and and_10 (and_10_out, A_qn, B_qn, C_q, d, e);
  and and_11 (and_11_out, A_qn, B_q, C_q, not_1_out, e);
  and and_12 (and_12_out, A_qn, B_q, C_qn, d, e);
  and and_13 (and_13_out, A_q, B_qn, C_qn, d, e);
  and and_14 (and_14_out, A_q, B_qn, C_q, not_1_out, e);
  and and_15 (and_15_out, A_q, B_q, C_q, d, e);
  and and_16 (and_16_out, A_q, B_q, C_qn, not_1_out, e);
  or or_1 (or_1_out, and_1_out, and_2_out, and_3_out, and_4_out);
  or or_2 (or_2_out, and_5_out, and_6_out, and_7_out, and_8_out);
  T_Flip_Flop A (.clk(clock_1_out), .T(or_1_out), .Q(A_q), .Qn(A_qn));  // open: preset, reset, en
  T_Flip_Flop B (.clk(clock_1_out), .T(or_2_out), .Q(B_q), .Qn(B_qn));  // open: preset, reset, en
  or or_3 (or_3_out, and_9_out, and_10_out, and_11_out, and_12_out, and_13_out, and_14_out, and_15_out, and_16_out);
  LED led_1 (.in(A_q));
  T_Flip_Flop C (.clk(clock_1_out), .T(or_3_out), .Q(C_q), .Qn(C_qn));  // open: preset, reset, en
  LED led_2 (.in(C_q));
  LED led_3 (.in(B_q));
endmodule
